# Fritzing sketch MB85_FRAM (saved by Fritzing 0.9.3b)
breadboards: 1

parts:
  Part1 = Arduino Micro (Rev3)  # not connected
  Part2 = I2C Non-Volatile FRAM 32KB
  Part3 = I2C Non-Volatile FRAM 32KB

nets:
  VCC: Part2.A0, Part2.VCC, Part3.VCC
  N1: Part2.SDA, Part3.SDA
  N2: Part2.SCL, Part3.SCL
  GND: Part2.GND, Part3.GND

custom parts:
  I2C Non-Volatile FRAM 32KB: With our I2C FRAM breakout board you can add some FRAM storage to your next DIY project. FRAM allows for a lower power usage and a faster write performance. It's excellent for low-power or inconsistent-power datalogging or data buffering where you want to stream data fast while also keeping the data when there's no power. Unlike Flash or EEPROM there's no pages to worry about. Each byte can be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
